# Fritzing sketch Controlling 1 DC motor via relay (2-directions) (saved by Fritzing 0.9.4)

parts:
  Part1 = Arduino Uno (Rev3)
  U1 = RELAY [package=relay-g5q]
  U2 = RELAY [package=relay-g5q]
  Q1 = NPN-Transistor [package="TO92 [THT]"]
  Q2 = NPN-Transistor [package="TO92 [THT]"]
  D2 = Schottky Diode [part_number=1N5817 package="300 mil [THT]"]
  M1 = DC Motor
  Power_plug1 = Power plug
  D1 = Schottky Diode [part_number=1N5817 package="300 mil [THT]"]
  S1 = Pushbutton [package="[SMD]"]
  S2 = Pushbutton [package="[SMD]"]
  R1 = Resistor [tolerance=±5% resistance=10k package="0805 [SMD]"]
  R2 = Resistor [tolerance=±5% resistance=10k package=THT]

nets:
  N1: Part1.GND, Q1.E, R1.Pin_0
  N2: Part1.D2, Q2.B
  N3: Part1.D3_PWM, Q1.B
  N4: Part1.D5_PWM, S1.Pin_1, S1.Pin_2, R2.Pin_1
  N5: Part1.D6_PWM, S2.Pin_1, S2.Pin_2, R1.Pin_1
  N6: Part1.5V, U2.COIL2
  N7: U1.COIL2, D1.cathode
  N8: U1.MAIN, M1.pin_1
  N9: U1.NO, Power_plug1.VCC
  N10: U1.NC, U2.NC, Power_plug1.GND
  N11: U2.MAIN, M1.pin_2
  N12: Q1.C, D2.anode
  N13: Q2.C, D1.anode

notes:
  6 Volt
